# Fritzing sketch anslutning_av_flera_lysdioder (saved by Fritzing 0.9.6b)
breadboards: 8

parts:
  A2 = Arduino Uno (Rev3)
  R2 = Resistor [tolerance=±5% power=0.25 resistance=1k package=THT]
  LED2 = LED - 5mm [color="Red (633nm)" current=0.030 package="5 mm [THT]"]
  A3 = Arduino Uno (Rev3)
  LED3 = LED - 5mm [color="Red (633nm)" current=0.030 package="5 mm [THT]"]
  R3 = Resistor [tolerance=±5% power=0.25 resistance=1k package=THT]
  A4 = Arduino Uno (Rev3)
  LED4 = LED - 5mm [color="Red (633nm)" current=0.030 package="5 mm [THT]"]
  R4 = Resistor [tolerance=±5% power=0.25 resistance=1k package=THT]
  R5 = Resistor [tolerance=±5% power=0.25 resistance=1k package=THT]
  LED5 = LED - 5mm [color="Red (633nm)" current=0.030 package="5 mm [THT]"]
  A5 = Arduino Uno (Rev3)
  LED6 = LED - 5mm [color="Red (633nm)" current=0.030 package="5 mm [THT]"]
  LED7 = LED - 5mm [color="Red (633nm)" current=0.030 package="5 mm [THT]"]
  R6 = Resistor [tolerance=±5% power=0.25 resistance=1k package=THT]
  R7 = Resistor [tolerance=±5% power=0.25 resistance=1k package=THT]
  LED8 = LED - 5mm [color="Red (633nm)" current=0.030 package="5 mm [THT]"]
  R8 = Resistor [tolerance=±5% power=0.25 resistance=1k package=THT]
  A6 = Arduino Uno (Rev3)
  LED9 = LED - 5mm [color="Red (633nm)" current=0.030 package="5 mm [THT]"]
  R9 = Resistor [tolerance=±5% power=0.25 resistance=1k package=THT]
  A7 = Arduino Uno (Rev3)
  LED10 = LED - 5mm [color="Red (633nm)" current=0.030 package="5 mm [THT]"]
  R10 = Resistor [tolerance=±5% power=0.25 resistance=1k package=THT]
  LED11 = LED - 5mm [color="Red (633nm)" current=0.030 package="5 mm [THT]"]
  R11 = Resistor [tolerance=±5% power=0.25 resistance=1k package=THT]
  A8 = Arduino Uno (Rev3)
  LED12 = LED - 5mm [color="Red (633nm)" current=0.030 package="5 mm [THT]"]
  LED13 = LED - 5mm [color="Red (633nm)" current=0.030 package="5 mm [THT]"]
  R12 = Resistor [tolerance=±5% power=0.25 resistance=1k package=THT]
  R13 = Resistor [tolerance=±5% power=0.25 resistance=1k package=THT]
  R14 = Resistor [tolerance=±5% power=0.25 resistance=1k package=THT]
  LED14 = LED - 5mm [color="Red (633nm)" current=0.030 package="5 mm [THT]"]
  A9 = Arduino Uno (Rev3)  # not connected

nets:
  N1: A2.5V, LED2.anode
  N2: A2.GND, R2.Pin_1
  N3: R2.Pin_0, LED2.cathode
  N4: A3.5V, LED3.anode
  N5: A3.GND, R3.Pin_1
  N6: LED3.cathode, R3.Pin_0
  N7: A4.5V, LED4.anode, LED5.anode
  N8: A4.GND, R4.Pin_1, R5.Pin_1
  N9: LED4.cathode, R4.Pin_0
  N10: R5.Pin_0, LED5.cathode
  N11: A5.5V, LED6.anode, LED7.anode, LED8.anode
  N12: A5.GND, R6.Pin_1, R7.Pin_1, R8.Pin_1
  N13: LED6.cathode, R6.Pin_0
  N14: LED7.cathode, R7.Pin_0
  N15: LED8.cathode, R8.Pin_0
  N16: A6.5V, LED9.anode
  N17: A6.GND, R9.Pin_1
  N18: LED9.cathode, R9.Pin_0
  N19: A7.5V, LED10.anode, LED11.anode
  N20: A7.GND, R10.Pin_1, R11.Pin_1
  N21: LED10.cathode, R10.Pin_0
  N22: LED11.cathode, R11.Pin_0
  N23: A8.5V, LED12.anode, LED13.anode, LED14.anode
  N24: A8.GND, R12.Pin_1, R13.Pin_1, R14.Pin_1
  N25: LED12.cathode, R12.Pin_0
  N26: LED13.cathode, R13.Pin_0
  N27: R14.Pin_0, LED14.cathode
