# Fritzing sketch maetning_av_en_servo (saved by Fritzing 1.0.1rc)
breadboards: 1

parts:
  OM1 = Multimeter (Ohmmeter)
  P1 = Multimeter straight black probe
  P2 = Multimeter straight red probe
  R6 = Photocell (LDR) [package=THT]
  Part1 = Arduino Uno (Rev3)
  R7 = Photocell (LDR) [package=THT]
  R8 = Resistor [tolerance=±5% power=0.25 resistance=1000 package=THT]
  P4 = Multimeter straight red probe
  P5 = Multimeter straight black probe

nets:
  N1: OM1.COM_Probe, P1.Probe_meter_end, P1.Probe_tip_2, R6.pin_1
  N2: OM1.V_Probe, P2.Probe_meter_end, P2.Probe_tip_2
  N3: Part1.5V, R7.pin_0
  N4: Part1.GND, R8.Pin_1, P5.Probe_tip, P5.Probe_meter_end
  N5: R7.pin_1, R8.Pin_0, P4.Probe_tip, P4.Probe_meter_end, P4.Probe_tip_2
