# Fritzing sketch 23_ansluting_av_en_relae_h_bridge (saved by Fritzing 1.0.1rc)
breadboards: 2

parts:
  VCC2 = Battery block 9V [internal_resistance=0.1Ω]
  R2 = Resistor [tolerance=±5% resistance=1000 package="0805 [SMD]"]
  LED2 = LED - 5mm [color="Blue (470nm)" current=0.030 package="5 mm [THT]"]
  U2 = 4-Channel 5v Relay Shield [package=relay-4ch5v10a]
  LED3 = LED - 5mm [color="Green (555nm)" current=0.030 package="5 mm [THT]"]
  VCC3 = Battery block 9V [internal_resistance=0.1Ω]
  R3 = Resistor [tolerance=±5% resistance=1000 package="0805 [SMD]"]
  LED4 = LED - 5mm [color="Green (555nm)" current=0.030 package="5 mm [THT]"]
  LED5 = LED - 5mm [color="Blue (470nm)" current=0.030 package="5 mm [THT]"]

nets:
  N1: VCC2.-, U2.K1-Off, U2.K3-Off
  N2: VCC2.+, R2.Pin_0
  N3: R2.Pin_1, U2.K2-On, U2.K4-On
  N4: LED2.cathode, U2.K1-On, U2.K4-Off, LED3.anode
  N5: LED2.anode, U2.K2-Off, U2.K3-On, LED3.cathode
  N6: VCC3.-, LED4.anode, LED5.cathode
  N7: VCC3.+, R3.Pin_0
  N8: R3.Pin_1, LED4.cathode, LED5.anode

custom parts:
  4-Channel 5v Relay Shield: 4 Channel 5v Relay Shield w. 2x SPD-06VDC-SD-C
