# Fritzing sketch 24_anvaendning_av_ett_relae (saved by Fritzing 1.0.1rc)
breadboards: 2

parts:
  U1 = 4-Channel 5v Relay Shield [package=relay-4ch5v10a]
  Part1 = Arduino Uno (Rev3)
  VCC1 = Battery block 9V [internal_resistance=0.1Ω]
  R1 = Resistor [tolerance=±5% resistance=1000 package="0805 [SMD]"]
  LED1 = LED - 5mm [color="Red (633nm)" current=0.030 package="5 mm [THT]"]
  Part2 = Arduino Uno (Rev3)
  VCC2 = Battery block 9V [internal_resistance=0.1Ω]
  R2 = Resistor [tolerance=±5% resistance=1000 package="0805 [SMD]"]
  LED2 = LED - 5mm [color="Blue (470nm)" current=0.030 package="5 mm [THT]"]
  U2 = 4-Channel 5v Relay Shield [package=relay-4ch5v10a]
  LED3 = LED - 5mm [color="Green (555nm)" current=0.030 package="5 mm [THT]"]

nets:
  VCC: U1.VCC, Part1.5V
  GND: U1.GND, Part1.GND
  N1: U1.IN1, Part1.D13/SCK
  N2: U1.K1-Off, VCC1.-
  N3: U1.K1-On, R1.Pin_1
  N4: VCC1.+, LED1.anode
  N5: R1.Pin_0, LED1.cathode
  N6: Part2.D10_PWM/SS, U2.IN1
  N7: Part2.D11_PWM/MOSI, U2.IN2
  N8: Part2.D12/MISO, U2.IN3
  N9: Part2.D13/SCK, U2.IN4
  5V: Part2.5V, U2.VCC
  GND_2: Part2.GND, U2.GND
  N10: VCC2.-, U2.K1-Off, U2.K3-Off
  N11: R2.Pin_1, U2.K2-On, U2.K4-On
  N12: LED2.cathode, U2.K1-On, U2.K4-Off, LED3.anode
  N13: LED2.anode, U2.K2-Off, U2.K3-On, LED3.cathode

custom parts:
  4-Channel 5v Relay Shield: 4 Channel 5v Relay Shield w. 2x SPD-06VDC-SD-C
