# Fritzing sketch 28_maetning_av_en_avstaandssensor (saved by Fritzing 1.0.1rc)
breadboards: 1

parts:
  P6 = Multimeter straight black probe
  Mod1 = KY-032 IR Obstacle Avoidance Sensor Module [package="Breakout board"]
  Part1 = Arduino Uno (Rev3)

nets:
  N1: P6.Probe_tip, P6.Probe_meter_end, Mod1.out
  GND: Mod1.GND, Part1.GND
  N2: Mod1.+, Part1.5V

notes:
  Part from https://arduinomodules.info/download/ky-032-infrared-obstacle-avoidance-sensor-module-zip-file/
  GND + Out EN
  https://github.com/kaitlynfranz/Digilent_Fritzing_Parts
  Till oscilloskopen

custom parts:
  KY-032 IR Obstacle Avoidance Sensor Module: KY-032 Infrared Obstacle Avoidance Sensor. Distance-adjustable, infrared proximity sensor designed for wheeled robots. Also known as AD-032.
