# Fritzing sketch 36_anvaendning_av_en_kapacitiv_knapp_1 (saved by Fritzing 1.0.1rc)
circuit board: 8.46667cm x 5.64444cm
breadboards: 1

parts:
  Part1 = Arduino Uno (Rev3)
  R_hulp = Resistor [tolerance=±5% resistance=1M power=0.25 package=THT]
  R_sensor = Resistor [tolerance=±5% resistance=1k power=0.25 package=THT]
  R_knop = Resistor [tolerance=±5% resistance=0 power=0.25 package=THT]

nets:
  N1: Part1.D2, R_hulp.Pin_0
  N2: Part1.D4, R_sensor.Pin_1
  N3: R_hulp.Pin_1, R_sensor.Pin_0, R_knop.Pin_0

notes:
  1 mega Ohm
  Brun svart grön guld
  1 kilo Ohm
  Brun svart grön guld
