# Fritzing sketch anvaendning_av_en_lcd (saved by Fritzing 1.0.1rc)
circuit board: 31.677cm x 14.8245cm
breadboards: 1

parts:
  Part2 = Arduino Uno (Rev3)
  LCD2 = LCD screen
  R1 = Rotary Potentiometer (Small) [maximum_resistance=100kΩ knob_status=50% package=THT]

nets:
  N1: Part2.D11_PWM/MOSI, LCD2.E
  N2: Part2.D12/MISO, LCD2.RS
  GND: Part2.GND, LCD2.VSS, LCD2.R/W, LCD2.LED-, R1.leg1
  N3: Part2.D2, LCD2.DB7
  N4: Part2.D3_PWM, LCD2.DB6
  N5: Part2.D4, LCD2.DB5
  N6: Part2.D5_PWM, LCD2.DB4
  5V: Part2.5V, LCD2.VDD, LCD2.LED+, R1.leg2
  N7: LCD2.V0, R1.wiper
