# Fritzing sketch 08_ldr (saved by Fritzing 0.9.3b)
breadboards: 2

parts:
  Part1 = Arduino Uno (Rev3)
  R1 = Rotary Potentiometer (Small) [maximum_resistance=100kΩ package=THT]
  Part2 = Arduino Uno (Rev3)
  R2 = Photocell (LDR) [package=THT]
  R3 = Resistor [tolerance=±5% resistance=10k package=THT]

nets:
  N1: Part1.A0, R1.wiper
  N2: Part1.5V, R1.leg1
  N3: Part1.GND, R1.leg2
  N4: Part2.A0, R2.pin_1, R3.Pin_0
  N5: Part2.5V, R2.pin_0
  N6: Part2.GND, R3.Pin_1
