# Fritzing sketch 01_anslutning_av_en_lysdiod (saved by Fritzing 0.9.6b)
breadboards: 4

parts:
  A1 = Arduino Uno (Rev3)
  LED1 = LED - 5mm [color="Red (633nm)" current=0.030 package="5 mm [THT]"]
  R1 = Resistor [tolerance=±5% power=0.25 resistance=1k package=THT]
  A2 = Arduino Uno (Rev3)
  R2 = Resistor [tolerance=±5% power=0.25 resistance=1k package=THT]
  LED2 = LED - 5mm [color="Red (633nm)" current=0.030 package="5 mm [THT]"]
  A3 = Arduino Uno (Rev3)
  LED3 = LED - 5mm [color="Red (633nm)" current=0.030 package="5 mm [THT]"]
  R3 = Resistor [tolerance=±5% power=0.25 resistance=1k package=THT]
  A4 = Arduino Uno (Rev3)
  A5 = Arduino Uno (Rev3)
  LED4 = LED - 5mm [color="Red (633nm)" current=0.030 package="5 mm [THT]"]
  LED5 = LED - 5mm [color="Red (633nm)" current=0.030 package="5 mm [THT]"]
  R4 = Resistor [tolerance=±5% power=0.25 resistance=1k package=THT]
  R5 = Resistor [tolerance=±5% power=0.25 resistance=1k package=THT]
  A6 = Arduino Uno (Rev3)
  LED6 = LED - 5mm [color="Red (633nm)" current=0.030 package="5 mm [THT]"]
  R6 = Resistor [tolerance=±5% power=0.25 resistance=1k package=THT]
  A7 = Arduino Uno (Rev3)
  A8 = Arduino Uno (Rev3)
  LED7 = LED - 5mm [color="Red (633nm)" current=0.030 package="5 mm [THT]"]
  LED8 = LED - 5mm [color="Red (633nm)" current=0.030 package="5 mm [THT]"]
  R7 = Resistor [tolerance=±5% power=0.25 resistance=1k package=THT]
  R8 = Resistor [tolerance=±5% power=0.25 resistance=1k package=THT]
  R9 = Resistor [tolerance=±5% power=0.25 resistance=1k package=THT]
  OM1 = Multimeter (Ohmmeter)
  P1 = Multimeter straight red probe
  P2 = Multimeter straight black probe
  R10 = Resistor [tolerance=±5% power=0.25 resistance=10k package=THT]
  OM2 = Multimeter (Ohmmeter)
  P3 = Multimeter straight red probe
  P4 = Multimeter straight black probe
  R11 = Resistor [tolerance=±5% power=0.25 resistance=10k package=THT]  # not connected
  R12 = Resistor [tolerance=±5% power=0.25 resistance=1k package=THT]  # not connected
  OM3 = Multimeter (Ohmmeter)
  OM4 = Multimeter (Ohmmeter)
  P5 = Multimeter straight red probe
  P6 = Multimeter straight red probe
  P7 = Multimeter straight black probe
  P8 = Multimeter straight black probe

nets:
  N1: A1.5V, LED1.anode
  N2: A1.GND, R1.Pin_1
  N3: LED1.cathode, R1.Pin_0
  N4: A2.5V, LED2.anode
  N5: A2.GND, R2.Pin_1
  N6: R2.Pin_0, LED2.cathode
  N7: A3.5V, LED3.cathode
  N8: A3.GND, R3.Pin_1
  N9: LED3.anode, R3.Pin_0
  N10: A4.5V, LED4.anode
  N11: A4.GND, R4.Pin_0
  N12: A5.5V, LED5.cathode
  N13: A5.GND, R5.Pin_0
  N14: LED4.cathode, R4.Pin_1
  N15: LED5.anode, R5.Pin_1
  N16: A6.5V, LED6.cathode
  N17: A6.GND, R6.Pin_1
  N18: LED6.anode, R6.Pin_0
  N19: A7.5V, LED8.anode
  N20: A7.GND, R8.Pin_0
  N21: A8.5V, LED7.cathode
  N22: A8.GND, R7.Pin_0
  N23: LED7.anode, R7.Pin_1
  N24: LED8.cathode, R8.Pin_1
  N25: R9.Pin_0, OM1.V_Probe, P1.Probe_meter_end, P1.Probe_tip_2
  N26: R9.Pin_1, OM1.COM_Probe, P2.Probe_meter_end, P2.Probe_tip_2
  N27: R10.Pin_0, OM2.V_Probe, P3.Probe_meter_end, P3.Probe_tip_2
  N28: R10.Pin_1, OM2.COM_Probe, P4.Probe_meter_end, P4.Probe_tip_2
  N29: OM3.COM_Probe, P7.Probe_meter_end
  N30: OM3.V_Probe, P5.Probe_meter_end
  N31: OM4.COM_Probe, P8.Probe_meter_end
  N32: OM4.V_Probe, P6.Probe_meter_end
