# Fritzing sketch 1_Blink_op_12 (saved by Fritzing 0.9.3b)
circuit board: 8cm x 6cm
breadboards: 1

parts:
  R1 = Resistor [tolerance=±5% resistance=1k package=THT]
  A1 = Arduino Uno (Rev3)
  LED1 = LED - 5mm [color="Red (633nm)" package="5 mm [THT]"]

nets:
  N1: R1.Pin_0, LED1.cathode
  N2: R1.Pin_1, A1.GND
  N3: A1.D12/MISO, LED1.anode

notes:
  1000 Ohm
  Brun
  Svart
  Röd
  Guld
