# Fritzing sketch 02_anvaendning_av_en_lysdiod (saved by Fritzing 0.9.6b)
breadboards: 2

parts:
  A2 = Arduino Uno (Rev3)
  R2 = Resistor [tolerance=±5% power=0.25 resistance=1k package=THT]
  LED2 = LED - 5mm [color="Red (633nm)" current=0.030 package="5 mm [THT]"]
  A3 = Arduino Uno (Rev3)
  LED3 = LED - 5mm [color="Red (633nm)" current=0.030 package="5 mm [THT]"]
  R3 = Resistor [tolerance=±5% power=0.25 resistance=1k package=THT]

nets:
  N1: A2.5V, LED2.anode
  N2: A2.GND, R2.Pin_1
  N3: R2.Pin_0, LED2.cathode
  N4: A3.D13/SCK, LED3.anode
  N5: A3.GND, R3.Pin_1
  N6: LED3.cathode, R3.Pin_0
