# Fritzing sketch anvaendning_av_en_multimeter (saved by Fritzing 0.9.6b)

parts:
  R9 = Resistor [tolerance=±5% power=0.25 resistance=1k package=THT]
  OM1 = Multimeter (Ohmmeter)
  P1 = Multimeter straight red probe
  P2 = Multimeter straight black probe
  R10 = Resistor [tolerance=±5% power=0.25 resistance=10k package=THT]
  OM2 = Multimeter (Ohmmeter)
  P3 = Multimeter straight red probe
  P4 = Multimeter straight black probe
  R11 = Resistor [tolerance=±5% power=0.25 resistance=10k package=THT]
  R12 = Resistor [tolerance=±5% power=0.25 resistance=1k package=THT]
  OM3 = Multimeter (Ohmmeter)
  OM4 = Multimeter (Ohmmeter)
  P5 = Multimeter straight red probe
  P6 = Multimeter straight red probe
  P7 = Multimeter straight black probe
  P8 = Multimeter straight black probe
  OM5 = Multimeter (Ohmmeter)
  OM6 = Multimeter (Ohmmeter)
  P9 = Multimeter straight red probe
  P10 = Multimeter straight red probe
  P11 = Multimeter straight black probe
  P12 = Multimeter straight black probe
  LED2 = LED - 5mm [color="Red (633nm)" current=0.030 package="5 mm [THT]"]  # not connected
  LED3 = LED - 5mm [color="Red (633nm)" current=0.030 package="5 mm [THT]"]
  OM7 = Multimeter (Ohmmeter)
  OM8 = Multimeter (Ohmmeter)
  P13 = Multimeter straight red probe
  P14 = Multimeter straight red probe
  P15 = Multimeter straight black probe
  P16 = Multimeter straight black probe

nets:
  N1: R9.Pin_0, OM1.V_Probe, P1.Probe_tip, P1.Probe_meter_end, P1.Probe_tip_2
  N2: R9.Pin_1, OM1.COM_Probe, P2.Probe_tip, P2.Probe_meter_end, P2.Probe_tip_2
  N3: R10.Pin_0, OM2.V_Probe, P3.Probe_tip, P3.Probe_meter_end, P3.Probe_tip_2
  N4: R10.Pin_1, OM2.COM_Probe, P4.Probe_tip, P4.Probe_meter_end, P4.Probe_tip_2
  N5: R11.Pin_0, OM4.COM_Probe, P8.Probe_tip, P8.Probe_meter_end, P8.Probe_tip_2
  N6: R12.Pin_1, OM3.V_Probe, P5.Probe_tip, P5.Probe_meter_end, P5.Probe_tip_2
  N7: OM3.COM_Probe, P7.Probe_meter_end
  N8: OM4.V_Probe, P6.Probe_meter_end
  N9: OM5.COM_Probe, P11.Probe_tip, P11.Probe_meter_end, P11.Probe_tip_2, LED3.cathode
  N10: OM5.V_Probe, P9.Probe_meter_end
  N11: OM6.COM_Probe, P12.Probe_meter_end
  N12: OM6.V_Probe, P10.Probe_meter_end
  N13: OM7.COM_Probe, P15.Probe_meter_end
  N14: OM7.V_Probe, P13.Probe_meter_end
  N15: OM8.COM_Probe, P16.Probe_meter_end
  N16: OM8.V_Probe, P14.Probe_meter_end
