# Fritzing sketch 02_blink_blink_blink (saved by Fritzing 0.9.3b)
circuit board: 8.46667cm x 5.64444cm
breadboards: 1

parts:
  R1 = Resistor [tolerance=±5% resistance=1k package=THT]
  LED1 = LED - 5mm [color="Red (633nm)" package="5 mm [THT]"]
  R2 = Resistor [tolerance=±5% resistance=1k package=THT]
  LED2 = LED - 5mm [color="Green (555nm)" package="5 mm [THT]"]
  R3 = Resistor [tolerance=±5% resistance=1k package=THT]
  LED3 = LED - 5mm [color="Blue (430nm)" package="5 mm [THT]"]
  Arduino = Arduino Uno (Rev3)

nets:
  N1: R1.Pin_0, LED1.cathode
  N2: R1.Pin_1, R2.Pin_1, R3.Pin_1, Arduino.GND
  N3: LED1.anode, Arduino.D11_PWM/MOSI
  N4: R2.Pin_0, LED2.cathode
  N5: LED2.anode, Arduino.D10_PWM/SS
  N6: R3.Pin_0, LED3.cathode
  N7: LED3.anode, Arduino.D9_PWM

notes:
  1000 Ohm
  Brun Svart Röd Guld
