# Fritzing sketch anslutning_av_en_lysdiod (saved by Fritzing 0.9.6b)
breadboards: 17

parts:
  A1 = Arduino Uno (Rev3)
  LED1 = LED - 5mm [color="Red (633nm)" current=0.030 package="5 mm [THT]"]
  R1 = Resistor [tolerance=±5% power=0.25 resistance=1k package=THT]
  A2 = Arduino Uno (Rev3)
  R2 = Resistor [tolerance=±5% power=0.25 resistance=1k package=THT]
  LED2 = LED - 5mm [color="Red (633nm)" current=0.030 package="5 mm [THT]"]
  A3 = Arduino Uno (Rev3)
  LED3 = LED - 5mm [color="Red (633nm)" current=0.030 package="5 mm [THT]"]
  R3 = Resistor [tolerance=±5% power=0.25 resistance=1k package=THT]
  A4 = Arduino Uno (Rev3)
  A5 = Arduino Uno (Rev3)
  LED4 = LED - 5mm [color="Red (633nm)" current=0.030 package="5 mm [THT]"]
  LED5 = LED - 5mm [color="Red (633nm)" current=0.030 package="5 mm [THT]"]
  R4 = Resistor [tolerance=±5% power=0.25 resistance=1k package=THT]
  R5 = Resistor [tolerance=±5% power=0.25 resistance=1k package=THT]
  A6 = Arduino Uno (Rev3)
  LED6 = LED - 5mm [color="Red (633nm)" current=0.030 package="5 mm [THT]"]
  R6 = Resistor [tolerance=±5% power=0.25 resistance=1k package=THT]
  A7 = Arduino Uno (Rev3)
  A8 = Arduino Uno (Rev3)
  LED7 = LED - 5mm [color="Red (633nm)" current=0.030 package="5 mm [THT]"]
  LED8 = LED - 5mm [color="Red (633nm)" current=0.030 package="5 mm [THT]"]
  R7 = Resistor [tolerance=±5% power=0.25 resistance=1k package=THT]
  R8 = Resistor [tolerance=±5% power=0.25 resistance=1k package=THT]
  A9 = Arduino Uno (Rev3)  # not connected
  LED9 = LED - 5mm [color="Red (633nm)" current=0.030 package="5 mm [THT]"]  # not connected
  R9 = Resistor [tolerance=±5% power=0.25 resistance=1k package=THT]  # not connected
  A10 = Arduino Uno (Rev3)
  LED10 = LED - 5mm [color="Red (633nm)" current=0.030 package="5 mm [THT]"]
  R10 = Resistor [tolerance=±5% power=0.25 resistance=1k package=THT]
  A11 = Arduino Uno (Rev3)
  LED11 = LED - 5mm [color="Red (633nm)" current=0.030 package="5 mm [THT]"]
  R11 = Resistor [tolerance=±5% power=0.25 resistance=1k package=THT]
  A12 = Arduino Uno (Rev3)
  LED12 = LED - 5mm [color="Red (633nm)" current=0.030 package="5 mm [THT]"]
  R12 = Resistor [tolerance=±5% power=0.25 resistance=1k package=THT]
  A13 = Arduino Uno (Rev3)
  LED13 = LED - 5mm [color="Red (633nm)" current=0.030 package="5 mm [THT]"]
  R13 = Resistor [tolerance=±5% power=0.25 resistance=1k package=THT]
  A14 = Arduino Uno (Rev3)
  LED14 = LED - 5mm [color="Red (633nm)" current=0.030 package="5 mm [THT]"]
  R14 = Resistor [tolerance=±5% power=0.25 resistance=1k package=THT]
  A15 = Arduino Uno (Rev3)
  LED15 = LED - 5mm [color="Red (633nm)" current=0.030 package="5 mm [THT]"]
  R15 = Resistor [tolerance=±5% power=0.25 resistance=1k package=THT]
  A16 = Arduino Uno (Rev3)
  LED16 = LED - 5mm [color="Red (633nm)" current=0.030 package="5 mm [THT]"]
  R16 = Resistor [tolerance=±5% power=0.25 resistance=1k package=THT]
  A17 = Arduino Uno (Rev3)
  LED17 = LED - 5mm [color="Red (633nm)" current=0.030 package="5 mm [THT]"]
  R17 = Resistor [tolerance=±5% power=0.25 resistance=1k package=THT]
  A18 = Arduino Uno (Rev3)
  LED19 = LED - 5mm [color="Red (633nm)" current=0.030 package="5 mm [THT]"]
  R18 = Resistor [tolerance=±5% power=0.25 resistance=1k package=THT]
  A19 = Arduino Uno (Rev3)
  LED20 = LED - 5mm [color="Red (633nm)" current=0.030 package="5 mm [THT]"]
  R19 = Resistor [tolerance=±5% power=0.25 resistance=1k package=THT]
  A20 = Arduino Uno (Rev3)
  LED21 = LED - 5mm [color="Red (633nm)" current=0.030 package="5 mm [THT]"]
  R20 = Resistor [tolerance=±5% power=0.25 resistance=1k package=THT]

nets:
  N1: A1.5V, LED1.anode
  N2: A1.GND, R1.Pin_1
  N3: LED1.cathode, R1.Pin_0
  N4: A2.5V, LED2.anode
  N5: A2.GND, R2.Pin_1
  N6: R2.Pin_0, LED2.cathode
  N7: A3.5V, LED3.cathode
  N8: A3.GND, R3.Pin_1
  N9: LED3.anode, R3.Pin_0
  N10: A4.5V, LED4.anode
  N11: A4.GND, R4.Pin_0
  N12: A5.5V, LED5.cathode
  N13: A5.GND, R5.Pin_0
  N14: LED4.cathode, R4.Pin_1
  N15: LED5.anode, R5.Pin_1
  N16: A6.5V, LED6.cathode
  N17: A6.GND, R6.Pin_1
  N18: LED6.anode, R6.Pin_0
  N19: A7.5V, LED8.anode
  N20: A7.GND, R8.Pin_0
  N21: A8.5V, LED7.cathode
  N22: A8.GND, R7.Pin_0
  N23: LED7.anode, R7.Pin_1
  N24: LED8.cathode, R8.Pin_1
  N25: A10.5V, LED10.cathode
  N26: A10.GND, R10.Pin_1
  N27: LED10.anode, R10.Pin_0
  N28: A11.5V, LED11.cathode
  N29: A11.GND, R11.Pin_1
  N30: LED11.anode, R11.Pin_0
  N31: A12.5V, LED12.cathode
  N32: A12.GND, R12.Pin_1
  N33: LED12.anode, R12.Pin_0
  N34: A13.5V, LED13.cathode, R13.Pin_0
  N35: A13.GND, R13.Pin_1
  N36: A14.5V, LED14.cathode
  N37: A14.GND, R14.Pin_1
  N38: LED14.anode, R14.Pin_0
  N39: A15.5V, R15.Pin_0
  N40: A15.GND, LED15.anode
  N41: LED15.cathode, R15.Pin_1
  N42: A16.5V, R16.Pin_0
  N43: A16.GND, LED16.anode
  N44: LED16.cathode, R16.Pin_1
  N45: A17.5V, R17.Pin_0
  N46: A17.GND, LED17.anode
  N47: LED17.cathode, R17.Pin_1
  N48: A18.5V, LED19.cathode
  N49: A18.GND, R18.Pin_1
  N50: LED19.anode, R18.Pin_0
  N51: A19.5V, LED20.cathode
  N52: A19.GND, R19.Pin_1
  N53: LED20.anode, R19.Pin_0
  N54: A20.5V, LED21.cathode
  N55: A20.GND, R20.Pin_0
  N56: LED21.anode, R20.Pin_1
