# Fritzing sketch anvaendning_av_flera_lysdioder (saved by Fritzing 0.9.6b)
breadboards: 4

parts:
  A5 = Arduino Uno (Rev3)
  LED6 = LED - 5mm [color="Red (633nm)" current=0.030 package="5 mm [THT]"]
  LED7 = LED - 5mm [color="Red (633nm)" current=0.030 package="5 mm [THT]"]
  R6 = Resistor [tolerance=±5% power=0.25 resistance=1k package=THT]
  R7 = Resistor [tolerance=±5% power=0.25 resistance=1k package=THT]
  LED8 = LED - 5mm [color="Red (633nm)" current=0.030 package="5 mm [THT]"]
  R8 = Resistor [tolerance=±5% power=0.25 resistance=1k package=THT]
  A6 = Arduino Uno (Rev3)
  LED9 = LED - 5mm [color="Red (633nm)" current=0.030 package="5 mm [THT]"]
  LED10 = LED - 5mm [color="Red (633nm)" current=0.030 package="5 mm [THT]"]
  LED11 = LED - 5mm [color="Red (633nm)" current=0.030 package="5 mm [THT]"]
  R9 = Resistor [tolerance=±5% power=0.25 resistance=1k package=THT]
  R10 = Resistor [tolerance=±5% power=0.25 resistance=1k package=THT]
  R11 = Resistor [tolerance=±5% power=0.25 resistance=1k package=THT]
  A7 = Arduino Uno (Rev3)
  LED12 = LED - 5mm [color="Red (633nm)" current=0.030 package="5 mm [THT]"]
  LED13 = LED - 5mm [color="Red (633nm)" current=0.030 package="5 mm [THT]"]
  LED14 = LED - 5mm [color="Red (633nm)" current=0.030 package="5 mm [THT]"]
  R12 = Resistor [tolerance=±5% power=0.25 resistance=1k package=THT]
  R13 = Resistor [tolerance=±5% power=0.25 resistance=1k package=THT]
  R14 = Resistor [tolerance=±5% power=0.25 resistance=1k package=THT]
  A8 = Arduino Uno (Rev3)
  LED15 = LED - 5mm [color="Red (633nm)" current=0.030 package="5 mm [THT]"]
  LED16 = LED - 5mm [color="Red (633nm)" current=0.030 package="5 mm [THT]"]
  LED17 = LED - 5mm [color="Red (633nm)" current=0.030 package="5 mm [THT]"]
  R15 = Resistor [tolerance=±5% power=0.25 resistance=1k package=THT]
  R16 = Resistor [tolerance=±5% power=0.25 resistance=1k package=THT]
  R17 = Resistor [tolerance=±5% power=0.25 resistance=1k package=THT]

nets:
  N1: A5.5V, LED6.anode, LED7.anode, LED8.anode
  N2: A5.GND, R6.Pin_1, R7.Pin_1, R8.Pin_1
  N3: LED6.cathode, R6.Pin_0
  N4: LED7.cathode, R7.Pin_0
  N5: LED8.cathode, R8.Pin_0
  N6: A6.D13/SCK, LED10.anode
  N7: A6.5V, LED9.anode, LED11.anode
  N8: A6.GND, R9.Pin_1, R10.Pin_1, R11.Pin_1
  N9: LED9.cathode, R9.Pin_0
  N10: LED10.cathode, R10.Pin_0
  N11: LED11.cathode, R11.Pin_0
  N12: A7.D11_PWM/MOSI, LED14.anode
  N13: A7.D12/MISO, LED12.anode
  N14: A7.D13/SCK, LED13.anode
  N15: A7.GND, R12.Pin_1, R13.Pin_1, R14.Pin_1
  N16: LED12.cathode, R12.Pin_0
  N17: LED13.cathode, R13.Pin_0
  N18: LED14.cathode, R14.Pin_0
  N19: A8.D12/MISO, LED15.anode
  N20: A8.D13/SCK, LED16.anode
  N21: A8.5V, LED17.anode
  N22: A8.GND, R15.Pin_1, R16.Pin_1, R17.Pin_1
  N23: LED15.cathode, R15.Pin_0
  N24: LED16.cathode, R16.Pin_0
  N25: LED17.cathode, R17.Pin_0
