# Fritzing sketch maetning_av_en_knapp (saved by Fritzing 0.9.6b)

parts:
  OM1 = Multimeter (Ohmmeter)
  S12 = Pushbutton [package="[SMD]"]  # not connected
  P1 = Multimeter straight black probe
  P2 = Multimeter straight red probe
  S13 = Pushbutton [package="[SMD]"]  # not connected
  OM2 = Multimeter (Ohmmeter)
  P3 = Multimeter straight black probe
  P4 = Multimeter straight red probe
  S14 = Pushbutton [package="[SMD]"]  # not connected
  OM3 = Multimeter (Ohmmeter)
  P5 = Multimeter straight black probe
  P6 = Multimeter straight red probe
  S15 = Pushbutton [package="[SMD]"]  # not connected
  S16 = Pushbutton [package="[SMD]"]  # not connected
  S17 = Pushbutton [package="[SMD]"]  # not connected
  OM4 = Multimeter (Ohmmeter)
  OM5 = Multimeter (Ohmmeter)
  OM6 = Multimeter (Ohmmeter)
  P7 = Multimeter straight black probe
  P8 = Multimeter straight black probe
  P9 = Multimeter straight black probe
  P10 = Multimeter straight red probe
  P11 = Multimeter straight red probe
  P12 = Multimeter straight red probe

nets:
  N1: OM1.COM_Probe, P1.Probe_tip, P1.Probe_meter_end
  N2: OM1.V_Probe, P2.Probe_tip, P2.Probe_meter_end
  N3: OM2.COM_Probe, P3.Probe_tip, P3.Probe_meter_end
  N4: OM2.V_Probe, P4.Probe_tip, P4.Probe_meter_end
  N5: OM3.COM_Probe, P5.Probe_tip, P5.Probe_meter_end
  N6: OM3.V_Probe, P6.Probe_tip, P6.Probe_meter_end
  N7: OM4.COM_Probe, P7.Probe_tip, P7.Probe_meter_end
  N8: OM4.V_Probe, P10.Probe_tip, P10.Probe_meter_end
  N9: OM5.COM_Probe, P8.Probe_tip, P8.Probe_meter_end
  N10: OM5.V_Probe, P12.Probe_tip, P12.Probe_meter_end
  N11: OM6.COM_Probe, P9.Probe_tip, P9.Probe_meter_end
  N12: OM6.V_Probe, P11.Probe_tip, P11.Probe_meter_end
