# Fritzing sketch anslutning_av_en_knapp (saved by Fritzing 1.0.1rc)
breadboards: 8

parts:
  A5 = Arduino Uno (Rev3)
  LED6 = LED - 5mm [color="Red (633nm)" current=0.030 package="5 mm [THT]"]
  R6 = Resistor [tolerance=±5% power=0.25 resistance=1k package=THT]
  S1 = Pushbutton [package="[SMD]"]
  A6 = Arduino Uno (Rev3)
  LED7 = LED - 5mm [color="Red (633nm)" current=0.030 package="5 mm [THT]"]
  R7 = Resistor [tolerance=±5% power=0.25 resistance=1k package=THT]
  S2 = Pushbutton [package="[SMD]"]
  A7 = Arduino Uno (Rev3)
  LED8 = LED - 5mm [color="Red (633nm)" current=0.030 package="5 mm [THT]"]
  R8 = Resistor [tolerance=±5% power=0.25 resistance=1k package=THT]
  S3 = Pushbutton [package="[SMD]"]
  A8 = Arduino Uno (Rev3)
  LED9 = LED - 5mm [color="Red (633nm)" current=0.030 package="5 mm [THT]"]
  R9 = Resistor [tolerance=±5% power=0.25 resistance=1k package=THT]
  S4 = Pushbutton [package="[SMD]"]
  A9 = Arduino Uno (Rev3)
  LED10 = LED - 5mm [color="Red (633nm)" current=0.030 package="5 mm [THT]"]
  R10 = Resistor [tolerance=±5% power=0.25 resistance=1k package=THT]
  S5 = Pushbutton [package="[SMD]"]
  A10 = Arduino Uno (Rev3)
  LED11 = LED - 5mm [color="Red (633nm)" current=0.030 package="5 mm [THT]"]
  R11 = Resistor [tolerance=±5% power=0.25 resistance=1k package=THT]
  S6 = Pushbutton [package="[SMD]"]
  S7 = Pushbutton [package="[SMD]"]
  A11 = Arduino Uno (Rev3)
  LED12 = LED - 5mm [color="Red (633nm)" current=0.030 package="5 mm [THT]"]
  R12 = Resistor [tolerance=±5% power=0.25 resistance=1k package=THT]
  S8 = Pushbutton [package="[SMD]"]
  S9 = Pushbutton [package="[SMD]"]
  A12 = Arduino Uno (Rev3)
  LED13 = LED - 5mm [color="Red (633nm)" current=0.030 package="5 mm [THT]"]
  R13 = Resistor [tolerance=±5% power=0.25 resistance=1k package=THT]
  S10 = Pushbutton [package="[SMD]"]
  S11 = Pushbutton [package="[SMD]"]
  LED14 = LED - 5mm [color="Red (633nm)" current=0.030 package="5 mm [THT]"]
  R14 = Resistor [tolerance=±5% power=0.25 resistance=1k package=THT]
  LED15 = LED - 5mm [color="Red (633nm)" current=0.030 package="5 mm [THT]"]
  R15 = Resistor [tolerance=±5% power=0.25 resistance=1k package=THT]

nets:
  N1: A5.5V, LED6.anode
  N2: A5.GND, R6.Pin_1
  N3: LED6.cathode, R6.Pin_0
  N4: S1.Pin_1, S1.Pin_2
  N5: S1.Pin_3, S1.Pin_4
  N6: A6.5V, LED7.anode, S2.Pin_3, S2.Pin_4
  N7: A6.GND, R7.Pin_1
  N8: LED7.cathode, R7.Pin_0
  N9: S2.Pin_1, S2.Pin_2
  N10: A7.5V, S3.Pin_3, S3.Pin_4
  N11: A7.GND, R8.Pin_1
  N12: LED8.cathode, R8.Pin_0
  N13: LED8.anode, S3.Pin_1, S3.Pin_2
  N14: A8.5V, S4.Pin_3, S4.Pin_4
  N15: A8.GND, R9.Pin_1
  N16: LED9.cathode, R9.Pin_0
  N17: LED9.anode, S4.Pin_1, S4.Pin_2
  N18: A9.5V, S5.Pin_3, S5.Pin_4
  N19: A9.GND, R10.Pin_1
  N20: LED10.cathode, R10.Pin_0
  N21: LED10.anode, S5.Pin_1, S5.Pin_2
  N22: A10.5V, S7.Pin_3, S7.Pin_4
  N23: A10.GND, R11.Pin_1
  N24: LED11.cathode, R11.Pin_0
  N25: LED11.anode, S6.Pin_1, S6.Pin_2
  N26: S6.Pin_3, S6.Pin_4, S7.Pin_1, S7.Pin_2
  N27: A11.5V, S8.Pin_3, S8.Pin_4, S9.Pin_3, S9.Pin_4
  N28: A11.GND, R12.Pin_1
  N29: LED12.cathode, R12.Pin_0
  N30: LED12.anode, S8.Pin_1, S8.Pin_2, S9.Pin_1, S9.Pin_2
  N31: A12.5V, S10.Pin_3, S10.Pin_4, S11.Pin_3, S11.Pin_4
  N32: A12.GND, R13.Pin_1, R14.Pin_1, R15.Pin_1
  N33: LED13.cathode, R13.Pin_0
  N34: LED13.anode, S10.Pin_1, S10.Pin_2, S11.Pin_1, S11.Pin_2, LED14.anode, LED15.anode
  N35: LED14.cathode, R14.Pin_0
  N36: LED15.cathode, R15.Pin_0

notes:
  1k Ohm
  Rod Svart Brun Guld
