# Fritzing sketch anvaendning_av_en_knapp (saved by Fritzing 0.9.6b)
breadboards: 4

parts:
  A11 = Arduino Uno (Rev3)
  LED12 = LED - 5mm [color="Red (633nm)" current=0.030 package="5 mm [THT]"]
  R12 = Resistor [tolerance=±5% power=0.25 resistance=1k package=THT]
  S8 = Pushbutton [package="[SMD]"]
  S9 = Pushbutton [package="[SMD]"]
  LED13 = LED - 5mm [color="Red (633nm)" current=0.030 package="5 mm [THT]"]
  LED14 = LED - 5mm [color="Red (633nm)" current=0.030 package="5 mm [THT]"]
  R15 = Resistor [tolerance=±5% power=0.25 resistance=1k package=THT]
  R16 = Resistor [tolerance=±5% power=0.25 resistance=1k package=THT]
  A12 = Arduino Uno (Rev3)
  S10 = Pushbutton [package="[SMD]"]
  S11 = Pushbutton [package="[SMD]"]
  LED15 = LED - 5mm [color="Red (633nm)" current=0.030 package="5 mm [THT]"]
  LED16 = LED - 5mm [color="Red (633nm)" current=0.030 package="5 mm [THT]"]
  LED17 = LED - 5mm [color="Red (633nm)" current=0.030 package="5 mm [THT]"]
  R17 = Resistor [tolerance=±5% power=0.25 resistance=1k package=THT]
  R20 = Resistor [tolerance=±5% power=0.25 resistance=1k package=THT]
  R21 = Resistor [tolerance=±5% power=0.25 resistance=1k package=THT]
  A13 = Arduino Uno (Rev3)
  S12 = Pushbutton [package="[SMD]"]
  S13 = Pushbutton [package="[SMD]"]
  LED18 = LED - 5mm [color="Red (633nm)" current=0.030 package="5 mm [THT]"]
  LED19 = LED - 5mm [color="Red (633nm)" current=0.030 package="5 mm [THT]"]
  LED20 = LED - 5mm [color="Red (633nm)" current=0.030 package="5 mm [THT]"]
  R22 = Resistor [tolerance=±5% power=0.25 resistance=10k package=THT]
  R23 = Resistor [tolerance=±5% power=0.25 resistance=1k package=THT]
  R24 = Resistor [tolerance=±5% power=0.25 resistance=1k package=THT]
  R25 = Resistor [tolerance=±5% power=0.25 resistance=1k package=THT]
  R26 = Resistor [tolerance=±5% power=0.25 resistance=10k package=THT]
  A14 = Arduino Uno (Rev3)
  S14 = Pushbutton [package="[SMD]"]
  S15 = Pushbutton [package="[SMD]"]
  LED21 = LED - 5mm [color="Red (633nm)" current=0.030 package="5 mm [THT]"]
  R27 = Resistor [tolerance=±5% power=0.25 resistance=1k package=THT]
  R29 = Resistor [tolerance=±5% power=0.25 resistance=10k package=THT]
  R30 = Resistor [tolerance=±5% power=0.25 resistance=10k package=THT]

nets:
  N1: A11.5V, LED12.anode, S8.Pin_3, S8.Pin_4, S9.Pin_3, S9.Pin_4
  N2: A11.GND, R12.Pin_1, R15.Pin_1, R16.Pin_1
  N3: LED12.cathode, R12.Pin_0
  N4: S8.Pin_1, S8.Pin_2, LED14.anode
  N5: S9.Pin_1, S9.Pin_2, LED13.anode
  N6: LED13.cathode, R15.Pin_0
  N7: LED14.cathode, R16.Pin_0
  N8: A12.A0, S10.Pin_1, S10.Pin_2, LED16.anode
  N9: A12.A1, S11.Pin_1, S11.Pin_2, LED17.anode
  N10: A12.D13/SCK, LED15.anode
  N11: A12.5V, S10.Pin_3, S10.Pin_4, S11.Pin_3, S11.Pin_4
  N12: A12.GND, R17.Pin_1, R20.Pin_1, R21.Pin_1
  N13: LED15.cathode, R17.Pin_0
  N14: LED16.cathode, R20.Pin_0
  N15: LED17.cathode, R21.Pin_0
  N16: A13.A0, S12.Pin_1, S12.Pin_2, LED18.anode, R26.Pin_0
  N17: A13.A1, S13.Pin_1, S13.Pin_2, LED20.anode, R22.Pin_0
  N18: A13.D13/SCK, LED19.anode
  N19: A13.5V, S12.Pin_3, S12.Pin_4, S13.Pin_3, S13.Pin_4
  N20: A13.GND, R22.Pin_1, R23.Pin_1, R24.Pin_1, R25.Pin_1, R26.Pin_1
  N21: LED18.cathode, R25.Pin_0
  N22: LED19.cathode, R23.Pin_0
  N23: LED20.cathode, R24.Pin_0
  N24: A14.A0, S14.Pin_1, S14.Pin_2, R30.Pin_0
  N25: A14.A1, S15.Pin_1, S15.Pin_2, R29.Pin_0
  N26: A14.D13/SCK, LED21.anode
  N27: A14.5V, S14.Pin_3, S14.Pin_4, S15.Pin_3, S15.Pin_4
  N28: A14.GND, R27.Pin_1, R29.Pin_1, R30.Pin_1
  N29: LED21.cathode, R27.Pin_0
