# Fritzing sketch maetning_av_en_vridmotstaand (saved by Fritzing 0.9.6b)

parts:
  OM1 = Multimeter (Ohmmeter)
  P1 = Multimeter straight black probe
  P2 = Multimeter straight red probe
  R2 = Rotary Potentiometer (Small) [maximum_resistance=100kΩ package=THT]  # not connected
  OM2 = Multimeter (Ohmmeter)
  P3 = Multimeter straight black probe
  P4 = Multimeter straight red probe
  R3 = Rotary Potentiometer (Small) [maximum_resistance=100kΩ package=THT]  # not connected
  OM3 = Multimeter (Ohmmeter)
  P5 = Multimeter straight black probe
  P6 = Multimeter straight red probe
  R4 = Rotary Potentiometer (Small) [maximum_resistance=100kΩ package=THT]
  R5 = Rotary Potentiometer (Small) [maximum_resistance=100kΩ package=THT]  # not connected

nets:
  N1: OM1.COM_Probe, P1.Probe_meter_end, P1.Probe_tip_2
  N2: OM1.V_Probe, P2.Probe_meter_end, P2.Probe_tip_2
  N3: OM2.COM_Probe, P3.Probe_meter_end, P3.Probe_tip_2
  N4: OM2.V_Probe, P4.Probe_meter_end, P4.Probe_tip_2
  N5: OM3.COM_Probe, P5.Probe_meter_end, P5.Probe_tip_2
  N6: OM3.V_Probe, P6.Probe_meter_end, P6.Probe_tip_2, R4.wiper
