# Fritzing sketch anslutning_av_en_vridmotstaand (saved by Fritzing 0.9.6b)
breadboards: 7

parts:
  R2 = Rotary Potentiometer (Small) [maximum_resistance=100kΩ package=THT]  # not connected
  A6 = Arduino Uno (Rev3)
  LED7 = LED - 5mm [color="Red (633nm)" current=0.030 package="5 mm [THT]"]
  R7 = Resistor [tolerance=±5% power=0.25 resistance=1k package=THT]
  A7 = Arduino Uno (Rev3)
  R8 = Rotary Potentiometer (Small) [maximum_resistance=100kΩ package=THT]
  LED8 = LED - 5mm [color="Red (633nm)" current=0.030 package="5 mm [THT]"]
  R9 = Resistor [tolerance=±5% power=0.25 resistance=1k package=THT]
  A8 = Arduino Uno (Rev3)
  R10 = Rotary Potentiometer (Small) [maximum_resistance=100kΩ package=THT]
  LED9 = LED - 5mm [color="Red (633nm)" current=0.030 package="5 mm [THT]"]
  R11 = Resistor [tolerance=±5% power=0.25 resistance=1k package=THT]
  A9 = Arduino Uno (Rev3)
  R12 = Rotary Potentiometer (Small) [maximum_resistance=100kΩ package=THT]
  LED10 = LED - 5mm [color="Red (633nm)" current=0.030 package="5 mm [THT]"]
  R13 = Resistor [tolerance=±5% power=0.25 resistance=1k package=THT]
  A10 = Arduino Uno (Rev3)
  R14 = Rotary Potentiometer (Small) [maximum_resistance=100kΩ package=THT]
  LED11 = LED - 5mm [color="Red (633nm)" current=0.030 package="5 mm [THT]"]
  R15 = Resistor [tolerance=±5% power=0.25 resistance=1k package=THT]
  R16 = Rotary Potentiometer (Small) [maximum_resistance=100kΩ package=THT]
  A11 = Arduino Uno (Rev3)
  R17 = Rotary Potentiometer (Small) [maximum_resistance=100kΩ package=THT]
  R18 = Rotary Potentiometer (Small) [maximum_resistance=100kΩ package=THT]
  LED12 = LED - 5mm [color="Red (633nm)" current=0.030 package="5 mm [THT]"]
  R19 = Resistor [tolerance=±5% power=0.25 resistance=1k package=THT]
  A12 = Arduino Uno (Rev3)
  R20 = Rotary Potentiometer (Small) [maximum_resistance=100kΩ package=THT]
  R21 = Rotary Potentiometer (Small) [maximum_resistance=100kΩ package=THT]
  LED13 = LED - 5mm [color="Red (633nm)" current=0.030 package="5 mm [THT]"]
  R22 = Resistor [tolerance=±5% power=0.25 resistance=1k package=THT]

nets:
  N1: A6.5V, LED7.anode
  N2: A6.GND, R7.Pin_1
  N3: LED7.cathode, R7.Pin_0
  N4: A7.5V, R8.leg1
  N5: A7.GND, R9.Pin_1
  N6: R8.wiper, LED8.anode
  N7: LED8.cathode, R9.Pin_0
  N8: A8.5V, R10.leg1
  N9: A8.GND, R11.Pin_1
  N10: R10.leg2, LED9.anode
  N11: LED9.cathode, R11.Pin_0
  N12: A9.5V, R12.wiper
  N13: A9.GND, R13.Pin_1
  N14: R12.leg2, LED10.anode
  N15: LED10.cathode, R13.Pin_0
  N16: A10.5V, R14.leg1
  N17: A10.GND, R15.Pin_1
  N18: R14.wiper, R16.leg1
  N19: LED11.cathode, R15.Pin_0
  N20: LED11.anode, R16.wiper
  N21: A11.5V, R17.leg1
  N22: A11.GND, R19.Pin_1
  N23: R17.wiper, R18.wiper
  N24: R18.leg2, LED12.anode
  N25: LED12.cathode, R19.Pin_0
  N26: A12.5V, R20.wiper
  N27: A12.GND, R22.Pin_1
  N28: R20.leg2, R21.wiper
  N29: R21.leg2, LED13.anode
  N30: LED13.cathode, R22.Pin_0
