# Fritzing sketch anvaendning_av_en_vridmotstaand (saved by Fritzing 0.9.6b)
breadboards: 5

parts:
  A12 = Arduino Uno (Rev3)
  R20 = Rotary Potentiometer (Small) [maximum_resistance=100kΩ package=THT]
  R21 = Rotary Potentiometer (Small) [maximum_resistance=100kΩ package=THT]
  LED13 = LED - 5mm [color="Red (633nm)" current=0.030 package="5 mm [THT]"]
  R22 = Resistor [tolerance=±5% power=0.25 resistance=1k package=THT]
  LED14 = LED - 5mm [color="Red (633nm)" current=0.030 package="5 mm [THT]"]
  R23 = Resistor [tolerance=±5% power=0.25 resistance=1k package=THT]
  A13 = Arduino Uno (Rev3)
  R24 = Rotary Potentiometer (Small) [maximum_resistance=100kΩ package=THT]
  R25 = Rotary Potentiometer (Small) [maximum_resistance=100kΩ package=THT]
  LED15 = LED - 5mm [color="Red (633nm)" current=0.030 package="5 mm [THT]"]
  LED16 = LED - 5mm [color="Red (633nm)" current=0.030 package="5 mm [THT]"]
  R26 = Resistor [tolerance=±5% power=0.25 resistance=1k package=THT]
  R27 = Resistor [tolerance=±5% power=0.25 resistance=1k package=THT]
  A14 = Arduino Uno (Rev3)
  R28 = Rotary Potentiometer (Small) [maximum_resistance=100kΩ package=THT]
  R29 = Rotary Potentiometer (Small) [maximum_resistance=100kΩ package=THT]
  LED17 = LED - 5mm [color="Red (633nm)" current=0.030 package="5 mm [THT]"]
  LED18 = LED - 5mm [color="Red (633nm)" current=0.030 package="5 mm [THT]"]
  R30 = Resistor [tolerance=±5% power=0.25 resistance=1k package=THT]
  R31 = Resistor [tolerance=±5% power=0.25 resistance=1k package=THT]
  A16 = Arduino Uno (Rev3)
  R36 = Rotary Potentiometer (Small) [maximum_resistance=100kΩ package=THT]
  R37 = Rotary Potentiometer (Small) [maximum_resistance=100kΩ package=THT]
  LED21 = LED - 5mm [color="Red (633nm)" current=0.030 package="5 mm [THT]"]
  LED22 = LED - 5mm [color="Red (633nm)" current=0.030 package="5 mm [THT]"]
  R38 = Resistor [tolerance=±5% power=0.25 resistance=1k package=THT]
  R39 = Resistor [tolerance=±5% power=0.25 resistance=1k package=THT]
  A17 = Arduino Uno (Rev3)
  R40 = Rotary Potentiometer (Small) [maximum_resistance=100kΩ package=THT]
  R41 = Rotary Potentiometer (Small) [maximum_resistance=100kΩ package=THT]
  LED23 = LED - 5mm [color="Red (633nm)" current=0.030 package="5 mm [THT]"]
  LED24 = LED - 5mm [color="Red (633nm)" current=0.030 package="5 mm [THT]"]
  R42 = Resistor [tolerance=±5% power=0.25 resistance=1k package=THT]
  R43 = Resistor [tolerance=±5% power=0.25 resistance=1k package=THT]

nets:
  N1: A12.5V, R20.leg1, R21.leg2, LED13.anode, LED14.anode
  N2: A12.GND, R20.leg2, R21.leg1, R22.Pin_1, R23.Pin_1
  N3: LED13.cathode, R22.Pin_0
  N4: LED14.cathode, R23.Pin_0
  N5: A13.5V, R24.leg2, R25.leg1
  N6: A13.GND, R24.leg1, R25.leg2, R26.Pin_1, R27.Pin_1
  N7: R24.wiper, LED15.anode
  N8: R25.wiper, LED16.anode
  N9: LED15.cathode, R26.Pin_0
  N10: LED16.cathode, R27.Pin_0
  N11: A14.A0, R29.wiper
  N12: A14.A1, R28.wiper
  N13: A14.5V, R28.leg2, R29.leg1
  N14: A14.GND, R28.leg1, R29.leg2, R30.Pin_1, R31.Pin_1
  N15: LED17.cathode, R30.Pin_0
  N16: LED18.cathode, R31.Pin_0
  N17: A16.A0, R37.wiper
  N18: A16.A1, R36.wiper
  N19: A16.D10_PWM/SS, LED21.anode
  N20: A16.D11_PWM/MOSI, LED22.anode
  N21: A16.5V, R36.leg1, R37.leg1
  N22: A16.GND, R36.leg2, R37.leg2, R38.Pin_1, R39.Pin_1
  N23: LED21.cathode, R39.Pin_0
  N24: LED22.cathode, R38.Pin_0
  N25: A17.A0, R41.wiper
  N26: A17.A1, R40.wiper
  N27: A17.5V, R40.leg1, R41.leg1
  N28: A17.GND, R40.leg2, R41.leg2, R42.Pin_1, R43.Pin_1
  N29: LED23.cathode, R43.Pin_0
  N30: LED24.cathode, R42.Pin_0
