# Fritzing sketch maetning_av_en_joystick (saved by Fritzing 0.9.6b)

parts:
  P1 = Multimeter straight black probe
  P2 = Multimeter straight red probe
  joystick = Black Joystick KY-023
  Part1 = Arduino Uno (Rev3)
  P3 = Multimeter straight red probe
  Part2 = Arduino Uno (Rev3)
  P4 = Multimeter straight black probe
  P5 = Multimeter straight red probe
  joystick1 = Black Joystick KY-023
  U1 = BNC [package=bnc]  # not connected
  U2 = BNC [package=bnc]  # not connected
  U3 = BNC [package=bnc]  # not connected

nets:
  GND: P1.Probe_tip, P1.Probe_meter_end, P1.Probe_tip_2, joystick.GND, Part1.GND
  N1: P2.Probe_tip, P2.Probe_meter_end, P2.Probe_tip_2, joystick.VRx
  N2: joystick.VRy, P3.Probe_meter_end, P3.Probe_tip_2
  +5V: joystick.+5V, Part1.5V
  5V: Part2.5V, joystick1.+5V
  GND_2: Part2.GND, P4.Probe_tip, P4.Probe_meter_end, P4.Probe_tip_2, joystick1.GND
  N3: P5.Probe_tip, P5.Probe_meter_end, P5.Probe_tip_2, joystick1.VRx

notes:
  Joystick from
  https://github.com/peyretti/My-Templates-Fritzing
  or its Fork at
  https://github.com/richelbilderbeek/My-Templates-Fritzing
  CH1
  CH2

custom parts:
  Black Joystick KY-023: Description: The joystick is a combination of 2 analoog potentiometer and a digital switch. Arduino GND --> Module pin - Arduino +5V --> Module pin +5V Arduino Analoog 0 --> Module VRx Arduino Analoog 1 --> Module VRy Arduino Digital --> Module SW Dimensions: 1" x 1.25"
