# Fritzing sketch anslutning_av_en_joystick (saved by Fritzing 0.9.6b)
breadboards: 3

parts:
  Part2 = Arduino Uno (Rev3)
  joystick1 = Black Joystick KY-023
  LED1 = RGB LED (com. cathode, rgb) [package="5 mm [THT]"]
  R1 = Resistor [tolerance=±5% resistance=1k package="2010 [SMD]"]
  R2 = Resistor [tolerance=±5% resistance=1k package="2010 [SMD]"]
  R3 = Resistor [tolerance=±5% resistance=1k package="2010 [SMD]"]
  Part3 = Arduino Uno (Rev3)
  LED2 = RGB LED (com. cathode, rgb) [package="5 mm [THT]"]
  R4 = Resistor [tolerance=±5% resistance=1k package="2010 [SMD]"]
  R5 = Resistor [tolerance=±5% resistance=1k package="2010 [SMD]"]
  R6 = Resistor [tolerance=±5% resistance=1k package="2010 [SMD]"]
  joystick2 = Black Joystick KY-023
  Part4 = Arduino Uno (Rev3)
  LED3 = RGB LED (com. cathode, rgb) [package="5 mm [THT]"]
  R7 = Resistor [tolerance=±5% resistance=1k package="2010 [SMD]"]
  joystick3 = Black Joystick KY-023

nets:
  5V: Part2.5V, joystick1.+5V
  GND: Part2.GND, joystick1.GND, LED1.common_cathode
  N1: joystick1.SW, R3.Pin_0
  N2: joystick1.VRy, R2.Pin_0
  N3: joystick1.VRx, R1.Pin_0
  N4: LED1.red_anode, R1.Pin_1
  N5: LED1.green_anode, R2.Pin_1
  N6: LED1.blue_anode, R3.Pin_1
  5V_2: Part3.5V, R4.Pin_0, joystick2.SW, joystick2.+5V
  GND_2: Part3.GND, LED2.common_cathode, joystick2.GND
  N7: LED2.red_anode, R6.Pin_1
  N8: LED2.green_anode, R5.Pin_1
  N9: LED2.blue_anode, R4.Pin_1
  N10: R5.Pin_0, joystick2.VRy
  N11: R6.Pin_0, joystick2.VRx
  5V_3: Part4.5V, R7.Pin_0, joystick3.SW, joystick3.+5V
  GND_3: Part4.GND, LED3.common_cathode, joystick3.GND
  N12: LED3.blue_anode, R7.Pin_1

notes:
  Joystick from
  https://github.com/peyretti/My-Templates-Fritzing
  or its Fork at
  https://github.com/richelbilderbeek/My-Templates-Fritzing

custom parts:
  Black Joystick KY-023: Description: The joystick is a combination of 2 analoog potentiometer and a digital switch. Arduino GND --> Module pin - Arduino +5V --> Module pin +5V Arduino Analoog 0 --> Module VRx Arduino Analoog 1 --> Module VRy Arduino Digital --> Module SW Dimensions: 1" x 1.25"
