# Fritzing sketch anslutning_av_en_ldr (saved by Fritzing 1.0.1rc)
breadboards: 3

parts:
  Part1 = Arduino Uno (Rev3)
  Part2 = Arduino Uno (Rev3)
  R18 = Photocell (LDR) [package=THT]
  R19 = Resistor [tolerance=±5% power=0.25 resistance=1000 package=THT]
  R21 = Resistor [tolerance=±5% power=0.25 resistance=10k package=THT]
  LED4 = LED - 5mm [color="Red (633nm)" current=0.030 package="5 mm [THT]"]
  Part3 = Arduino Uno (Rev3)
  R23 = Photocell (LDR) [package=THT]
  R24 = Photocell (LDR) [package=THT]
  R25 = Resistor [tolerance=±5% power=0.25 resistance=1000 package=THT]
  R26 = Resistor [tolerance=±5% power=0.25 resistance=1k package=THT]
  R27 = Resistor [tolerance=±5% power=0.25 resistance=10k package=THT]
  R28 = Resistor [tolerance=±5% power=0.25 resistance=1000 package=THT]
  LED6 = LED - 5mm [color="Red (633nm)" current=0.030 package="5 mm [THT]"]
  LED7 = LED - 5mm [color="Red (633nm)" current=0.030 package="5 mm [THT]"]
  R7 = Photocell (LDR) [package=THT]
  LED1 = LED - 5mm [color="Red (633nm)" current=0.030 package="5 mm [THT]"]
  R9 = Resistor [tolerance=±5% power=0.25 resistance=1000 package=THT]
  R8 = Resistor [tolerance=±5% power=0.25 resistance=1k package=THT]

nets:
  N1: Part1.5V, R8.Pin_0
  N2: Part1.GND, R7.pin_1, R9.Pin_1
  N3: Part2.5V, R18.pin_0
  N4: Part2.GND, R19.Pin_1, R21.Pin_1
  N5: R18.pin_1, R21.Pin_0, LED4.anode
  N6: R19.Pin_0, LED4.cathode
  N7: Part3.5V, R24.pin_0, R26.Pin_0
  N8: Part3.GND, R23.pin_1, R25.Pin_1, R27.Pin_1, R28.Pin_1
  N9: R23.pin_0, R26.Pin_1, LED7.anode
  N10: R24.pin_1, R27.Pin_0, LED6.anode
  N11: R25.Pin_0, LED6.cathode
  N12: R28.Pin_0, LED7.cathode
  N13: R7.pin_0, LED1.anode, R8.Pin_1
  N14: LED1.cathode, R9.Pin_0

notes:
  10k Ohm
  brun svart orange gul
  1k Ohm
  brun svart röd
  gul
  1k Ohm
