# Fritzing sketch anvaendning_av_en_ldr (saved by Fritzing 1.0.1rc)
breadboards: 3

parts:
  Part2 = Arduino Uno (Rev3)
  R4 = Photocell (LDR) [package=THT]
  R5 = Resistor [tolerance=±5% power=0.25 resistance=1k package=THT]
  R6 = Photocell (LDR) [package=THT]
  R7 = Resistor [tolerance=±5% power=0.25 resistance=1k package=THT]
  R8 = Photocell (LDR) [package=THT]
  R9 = Resistor [tolerance=±5% power=0.25 resistance=1k package=THT]
  LED2 = RGB LED (com. cathode, rgb) [package="5 mm [THT]"]
  R10 = Resistor [tolerance=±5% resistance=1k package="2010 [SMD]"]
  R11 = Resistor [tolerance=±5% resistance=1k package="2010 [SMD]"]
  R12 = Resistor [tolerance=±5% resistance=1k package="2010 [SMD]"]
  Part3 = Arduino Uno (Rev3)
  LED3 = RGB LED (com. cathode, rgb) [package="5 mm [THT]"]
  R14 = Resistor [tolerance=±5% resistance=1k package="2010 [SMD]"]
  R15 = Resistor [tolerance=±5% resistance=1k package="2010 [SMD]"]
  R16 = Photocell (LDR) [package=THT]
  R18 = Photocell (LDR) [package=THT]
  R19 = Resistor [tolerance=±5% power=0.25 resistance=1000 package=THT]
  R20 = Resistor [tolerance=±5% power=0.25 resistance=1000 package=THT]
  Part4 = Arduino Uno (Rev3)
  LED4 = RGB LED (com. cathode, rgb) [package="5 mm [THT]"]
  R24 = Resistor [tolerance=±5% resistance=1k package="2010 [SMD]"]
  R25 = Photocell (LDR) [package=THT]
  R28 = Resistor [tolerance=±5% power=0.25 resistance=1000 package=THT]

nets:
  N1: Part2.A0, R4.pin_1, R5.Pin_0
  N2: Part2.A1, R6.pin_1, R7.Pin_0
  N3: Part2.A2, R8.pin_1, R9.Pin_0
  N4: Part2.D9_PWM, R12.Pin_0
  N5: Part2.D10_PWM/SS, R11.Pin_0
  N6: Part2.D11_PWM/MOSI, R10.Pin_0
  N7: Part2.5V, R4.pin_0, R6.pin_0, R8.pin_0
  N8: Part2.GND, R5.Pin_1, R7.Pin_1, R9.Pin_1, LED2.common_cathode
  N9: LED2.red_anode, R12.Pin_1
  N10: LED2.green_anode, R11.Pin_1
  N11: LED2.blue_anode, R10.Pin_1
  N12: Part3.A0, R16.pin_1, R19.Pin_0
  N13: Part3.A1, R18.pin_1, R20.Pin_0
  N14: Part3.D9_PWM, R15.Pin_0
  N15: Part3.D10_PWM/SS, R14.Pin_0
  N16: Part3.5V, R16.pin_0, R18.pin_0
  N17: Part3.GND, LED3.common_cathode, R19.Pin_1, R20.Pin_1
  N18: LED3.red_anode, R15.Pin_1
  N19: LED3.green_anode, R14.Pin_1
  N20: Part4.A0, R25.pin_1, R28.Pin_0
  N21: Part4.D9_PWM, R24.Pin_0
  N22: Part4.5V, R25.pin_0
  N23: Part4.GND, LED4.common_cathode, R28.Pin_1
  N24: LED4.red_anode, R24.Pin_1

notes:
  Alla: 1k Ohm
  brun svart röd guld
