# Fritzing sketch anslutning_av_en_servo (saved by Fritzing 1.0.1rc)

parts:
  Part2 = Arduino Uno (Rev3)
  J1 = Basic Servo
  P1 = Multimeter straight black probe
  P2 = Multimeter straight red probe

nets:
  5V: Part2.5V, J1.vcc
  GND: Part2.GND, J1.gnd, P1.Probe_tip, P1.Probe_meter_end
  N1: J1.pulse, P2.Probe_tip, P2.Probe_meter_end, P2.Probe_tip_2
