# Fritzing sketch 22_maetning_av_en_relais (saved by Fritzing 1.0.1rc)

parts:
  U1 = 4-Channel 5v Relay Shield [package=relay-4ch5v10a]
  Part1 = Arduino Uno (Rev3)
  P1 = Multimeter straight red probe
  P2 = Multimeter straight black probe
  OM1 = Multimeter (Ohmmeter)

nets:
  VCC: U1.VCC, Part1.5V
  GND: U1.GND, U1.IN1, Part1.GND
  N1: U1.K1-In, P2.Probe_tip, P2.Probe_meter_end, OM1.COM_Probe
  N2: U1.K1-Off, P1.Probe_tip, P1.Probe_meter_end, OM1.V_Probe

custom parts:
  4-Channel 5v Relay Shield: 4 Channel 5v Relay Shield w. 2x SPD-06VDC-SD-C
