# Fritzing sketch 23_ansluting_av_en_relae_led (saved by Fritzing 1.0.6)
breadboards: 2

parts:
  U1 = 4-Channel 5v Relay Shield [package=relay-4ch5v10a]
  Part1 = Arduino Uno (Rev3)
  VCC1 = Battery block 9V [internal_resistance=0.1Ω]
  R1 = Resistor [tolerance=±5% resistance=1000 package="0805 [SMD]"]
  LED1 = LED - 5mm [color="Red (633nm)" current=0.030 package="5 mm [THT]"]
  Part2 = Arduino Uno (Rev3)  # not connected
  VCC2 = Battery block 9V [internal_resistance=0.1Ω]
  R2 = Resistor [tolerance=±5% resistance=1000 package="0805 [SMD]"]
  LED2 = LED - 5mm [color="Blue (470nm)" current=0.030 package="5 mm [THT]"]
  U2 = 4-Channel 5v Relay Shield [package=relay-4ch5v10a]
  LED3 = LED - 5mm [color="Green (555nm)" current=0.030 package="5 mm [THT]"]

nets:
  VCC: U1.VCC, Part1.5V
  GND: U1.GND, U1.IN1, Part1.GND
  N1: U1.K1-Off, VCC1.-
  N2: U1.K1-On, R1.Pin_1
  N3: VCC1.+, LED1.anode
  N4: R1.Pin_0, LED1.cathode
  N5: VCC2.-, U2.K1-Off, U2.K3-Off
  N6: R2.Pin_1, U2.K2-On, U2.K4-On
  N7: LED2.cathode, U2.K1-On, U2.K4-Off, LED3.anode
  N8: LED2.anode, U2.K2-Off, U2.K3-On, LED3.cathode

custom parts:
  4-Channel 5v Relay Shield: 4 Channel 5v Relay Shield w. 2x SPD-06VDC-SD-C
