# Fritzing sketch 24_anvaendning_av_ett_relae (saved by Fritzing 1.0.1rc)
breadboards: 3

parts:
  Part2 = Arduino Uno (Rev3)
  VCC2 = Battery block 9V [internal_resistance=0.1Ω]
  R2 = Resistor [tolerance=±5% resistance=1000 package="0805 [SMD]"]
  LED2 = LED - 5mm [color="Blue (470nm)" current=0.030 package="5 mm [THT]"]
  U2 = 4-Channel 5v Relay Shield [package=relay-4ch5v10a]
  Part3 = Arduino Uno (Rev3)
  VCC3 = Battery block 9V [internal_resistance=0.1Ω]
  R3 = Resistor [tolerance=±5% resistance=1000 package="0805 [SMD]"]
  LED4 = LED - 5mm [color="Green (555nm)" current=0.030 package="5 mm [THT]"]
  LED5 = LED - 5mm [color="Blue (470nm)" current=0.030 package="5 mm [THT]"]
  U3 = 4-Channel 5v Relay Shield [package=relay-4ch5v10a]
  Part4 = Arduino Uno (Rev3)
  VCC4 = Battery block 9V [internal_resistance=0.1Ω]
  R4 = Resistor [tolerance=±5% resistance=1000 package="0805 [SMD]"]
  LED6 = LED - 5mm [color="Blue (470nm)" current=0.030 package="5 mm [THT]"]
  U4 = 4-Channel 5v Relay Shield [package=relay-4ch5v10a]

nets:
  N1: Part2.D10_PWM/SS, U2.IN1
  N2: Part2.D11_PWM/MOSI, U2.IN2
  5V: Part2.5V, U2.VCC
  GND: Part2.GND, U2.GND
  N3: VCC2.-, U2.K1-Off
  N4: VCC2.+, R2.Pin_0
  N5: R2.Pin_1, U2.K2-On
  N6: LED2.cathode, U2.K1-On
  N7: LED2.anode, U2.K2-Off
  N8: Part3.D10_PWM/SS, U3.IN1
  N9: Part3.D11_PWM/MOSI, U3.IN2
  N10: Part3.D12/MISO, U3.IN3
  N11: Part3.D13/SCK, U3.IN4
  5V_2: Part3.5V, U3.VCC
  GND_2: Part3.GND, U3.GND
  N12: VCC3.-, U3.K1-Off, U3.K3-Off
  N13: VCC3.+, R3.Pin_0
  N14: R3.Pin_1, U3.K2-On, U3.K4-On
  N15: LED4.cathode, LED5.anode, U3.K2-Off, U3.K3-On
  N16: LED4.anode, LED5.cathode, U3.K1-On, U3.K4-Off
  N17: Part4.D10_PWM/SS, U4.IN1
  5V_3: Part4.5V, U4.VCC, U4.IN4
  GND_3: Part4.GND, U4.GND
  N18: VCC4.-, U4.K1-Off
  N19: VCC4.+, R4.Pin_0
  N20: R4.Pin_1, LED6.anode
  N21: LED6.cathode, U4.K1-On

custom parts:
  4-Channel 5v Relay Shield: 4 Channel 5v Relay Shield w. 2x SPD-06VDC-SD-C
