# Fritzing sketch 25_maetning_av_en_dc_motor (saved by Fritzing 1.0.1rc)

parts:
  R1 = Photocell (LDR) [package=THT]  # not connected
  M1 = gear-motor
  VM1 = Multimeter (DC Voltage)
  P1 = Multimeter straight red probe
  P2 = Multimeter straight black probe
  R2 = Photocell (LDR) [package=THT]  # not connected
  P3 = Multimeter straight red probe
  P4 = Multimeter straight black probe
  VM2 = Multimeter (DC Voltage)
  VM3 = Multimeter (DC Voltage)
  P5 = Multimeter straight red probe
  P6 = Multimeter straight black probe

nets:
  N1: M1.pin_1, VM3.V_Probe, P5.Probe_meter_end, P5.Probe_tip_2
  N2: M1.pin_2, VM3.COM_Probe, P6.Probe_meter_end, P6.Probe_tip_2
  N3: VM1.COM_Probe, P2.Probe_meter_end, P2.Probe_tip_2
  N4: VM1.V_Probe, P1.Probe_meter_end, P1.Probe_tip_2
  N5: P3.Probe_meter_end, P3.Probe_tip_2, VM2.V_Probe
  N6: P4.Probe_meter_end, P4.Probe_tip_2, VM2.COM_Probe
