# Fritzing sketch 26_anslutning_av_en_dc_motor (saved by Fritzing 1.0.1rc)
breadboards: 6

parts:
  VCC3 = Battery block 9V [internal_resistance=0.1Ω]
  U3 = 4-Channel 5v Relay Shield [package=relay-4ch5v10a]
  M2 = DC Motor [voltage_(max)=6V voltage_(min)=3V]
  Part3 = Arduino Uno (Rev3)
  S5 = Pushbutton [package="[THT]"]
  S6 = Pushbutton [package="[THT]"]
  Part4 = Arduino Uno (Rev3)
  VCC4 = Battery block 9V [internal_resistance=0.1Ω]
  U4 = 4-Channel 5v Relay Shield [package=relay-4ch5v10a]
  M3 = DC Motor [voltage_(max)=6V voltage_(min)=3V]
  S7 = Pushbutton [package="[THT]"]
  Part5 = Arduino Uno (Rev3)
  VCC5 = Battery block 9V [internal_resistance=0.1Ω]
  U5 = 4-Channel 5v Relay Shield [package=relay-4ch5v10a]
  M4 = DC Motor [voltage_(max)=6V voltage_(min)=3V]
  S8 = Pushbutton [package="[THT]"]

nets:
  N1: VCC3.-, U3.K1-Off, U3.K3-Off
  N2: VCC3.+, U3.K2-On, U3.K4-On
  VCC: U3.VCC, Part3.5V
  GND: U3.GND, Part3.GND, S5.Pin_3, S5.Pin_4, S6.Pin_3, S6.Pin_4
  N3: U3.IN1, U3.IN2
  N4: U3.K1-On, U3.K4-Off, M2.pin_2
  N5: U3.K2-Off, U3.K3-On, M2.pin_1
  N6: U3.IN4, U3.IN3
  5V: Part4.5V, U4.VCC
  GND_2: Part4.GND, U4.GND, S7.Pin_3, S7.Pin_4
  N7: VCC4.-, U4.K1-Off
  N8: VCC4.+, U4.K2-On
  N9: U4.IN1, U4.IN2
  N10: U4.K1-On, M3.pin_2
  N11: U4.K2-Off, M3.pin_1
  5V_2: Part5.5V, U5.VCC
  GND_3: Part5.GND, U5.GND, S8.Pin_3, S8.Pin_4
  N12: VCC5.-, U5.K1-Off
  N13: VCC5.+, M4.pin_1
  N14: U5.K1-On, M4.pin_2

custom parts:
  4-Channel 5v Relay Shield: 4 Channel 5v Relay Shield w. 2x SPD-06VDC-SD-C
