# Fritzing sketch 30_anvaendning_av_en_avstaandssensor (saved by Fritzing 1.0.1rc)
breadboards: 1

parts:
  Mod1 = KY-032 IR Obstacle Avoidance Sensor Module [package="Breakout board"]
  Part1 = Arduino Uno (Rev3)
  R1 = Resistor [tolerance=±5% power=0.25 resistance=1000 package=THT]
  LED1 = LED - 5mm [color="Red (633nm)" current=0.030 package="5 mm [THT]"]

nets:
  GND: Mod1.GND, Part1.GND, R1.Pin_1
  N1: Mod1.+, Part1.5V
  N2: Mod1.out, Part1.D13/SCK
  N3: Part1.D12/MISO, LED1.anode
  N4: R1.Pin_0, LED1.cathode

notes:
  Part from https://arduinomodules.info/download/ky-032-infrared-obstacle-avoidance-sensor-module-zip-file/
  GND + Out EN
  https://github.com/kaitlynfranz/Digilent_Fritzing_Parts
  1000 Ohm
  Brun svart
  röd guld

custom parts:
  KY-032 IR Obstacle Avoidance Sensor Module: KY-032 Infrared Obstacle Avoidance Sensor. Distance-adjustable, infrared proximity sensor designed for wheeled robots. Also known as AD-032.
