# Fritzing sketch neo_pixel_1 (saved by Fritzing 0.9.6b)

parts:
  부품2 = Arduino Uno (Rev3)
  NEOPIXEL1 = Neopixel Strip -- Black (30/m)

nets:
  N1: 부품2.D6_PWM, NEOPIXEL1.DI
  5V: 부품2.5V, NEOPIXEL1.+5V
  GND: 부품2.GND, NEOPIXEL1.GND

custom parts:
  Neopixel Strip -- Black (30/m): Neopixel Strip, Black, 30 pixels per meter.
