# Fritzing sketch neo_pixel_2 (saved by Fritzing 1.0.1rc)

parts:
  부품2 = Arduino Uno (Rev3)
  NEOPIXEL1 = Neopixel Strip -- Black (30/m)
  NEOPIXEL2 = Neopixel Strip -- Black (30/m)
  부품3 = Arduino Uno (Rev3)
  NEOPIXEL3 = Neopixel Strip -- Black (30/m)
  NEOPIXEL4 = Neopixel Strip -- Black (30/m)
  AM1 = Multimeter (DC Current)

nets:
  N1: 부품2.D6_PWM, NEOPIXEL1.DI
  N2: 부품2.5V, NEOPIXEL1.+5V#1
  N3: 부품2.GND, NEOPIXEL1.GND#3
  N4: NEOPIXEL1.GND#4, NEOPIXEL2.GND
  N5: NEOPIXEL1.DO, NEOPIXEL2.DI
  N6: NEOPIXEL1.+5V#6, NEOPIXEL2.+5V
  N7: 부품3.D6_PWM, NEOPIXEL4.DI
  N8: 부품3.5V, NEOPIXEL4.+5V#1
  N9: 부품3.GND, AM1.COM_Probe
  N10: NEOPIXEL3.+5V, NEOPIXEL4.+5V#6
  N11: NEOPIXEL3.DI, NEOPIXEL4.DO
  N12: NEOPIXEL3.GND, NEOPIXEL4.GND#4
  N13: NEOPIXEL4.GND#3, AM1.A_Probe

custom parts:
  Neopixel Strip -- Black (30/m): Neopixel Strip, Black, 30 pixels per meter.
