# Fritzing sketch anvaendning_av_en_stegmotor (saved by Fritzing 1.0.1rc)
breadboards: 1

parts:
  Driver1 = 28BYJ-48 Driver Module [part_number=ULN2003 package=THT]
  SM1 = 28BYJ-48 Stepper Motor [part_number=28BYJ-48]
  Part1 = Arduino Uno (Rev3)
  VCC1 = Battery block 9V

nets:
  N1: Driver1.IN1, Part1.D11_PWM/MOSI
  N2: Driver1.IN2, Part1.D10_PWM/SS
  N3: Driver1.IN3, Part1.D9_PWM
  N4: Driver1.IN4, Part1.D8
  GND: Driver1.GND, Part1.GND, VCC1.-
  N5: Driver1.Vmotor, VCC1.+
  N6: Driver1.blue-pin, SM1.blue-pin
  N7: Driver1.pink-pin, SM1.pink-pin
  N8: Driver1.yellow-pin, SM1.yellow-pin
  N9: Driver1.orange-pin, SM1.orange-pin
  N10: Driver1.red-pin, SM1.red-pin

notes:
  https://github.com/mgesteiro/fritzing-parts/tree/main/28BYJ-48-driver
  https://github.com/mgesteiro/fritzing-parts/tree/main/28BYJ-48-motor

custom parts:
  28BYJ-48 Driver Module: ULN2003 Driver Module for the 28BYJ-48 Unipolar Stepper Motor LED A - Blue wire - Bottom coil left LED B - Pink wire - Top coil left LED C - Yellow wire - Bottom coil right LED D - Orange wire - Top coil right Common rail - red Connector pins: blue - pink - yellow - orange - red Control pins - IN1 to IN4 Power pins - GND & Vmotor (5-12V) On/Off jumper (if removed, power to motor is cut).
  28BYJ-48 Stepper Motor: Unipolar Stepper Motor 28BYJ-48 Top coil - pink & orange Bottom coil - blue & yellow Common rail - red Connector pins: blue - pink - yellow - orange - red
