# Fritzing sketch 34_maetning_av_en_kapacitiv_knapp (saved by Fritzing 1.0.1rc)
breadboards: 1

parts:
  Part1 = Arduino Uno (Rev3)
  R_hulp1 = Resistor [tolerance=±5% resistance=1M power=0.25 package=THT]
  R_sensor1 = Resistor [tolerance=±5% resistance=1k power=0.25 package=THT]
  R_knop1 = Resistor [tolerance=±5% resistance=0 power=0.25 package=THT]
  P1 = Multimeter straight black probe
  P2 = Multimeter straight red probe

nets:
  N1: Part1.5V, R_hulp1.Pin_0
  N2: Part1.GND, R_sensor1.Pin_1, P1.Probe_tip, P1.Probe_meter_end
  N3: R_hulp1.Pin_1, R_sensor1.Pin_0, R_knop1.Pin_0
  N4: R_knop1.Pin_1, P2.Probe_tip, P2.Probe_meter_end

notes:
  1 mega Ohm
  Brun Svart Grönt Guld
  1 kilo Ohm
  Brun Svart Röd Guld
