# Fritzing sketch bare_bone_arduino (saved by Fritzing 1.0.1rc)
circuit board: 8.46667cm x 5.64444cm

parts:
  U1 = atmega328 [package=dip]
  C2 = Capacitor [package=cap-pth-small2]
  C3 = Capacitor [package=cap-pth-small2]
  Y1 = CRYSTAL [package=crystal-smd-10.5x4.8-2pin]
  VCC1 = 4 x AAA Battery Mount

nets:
  N1: U1.VCC, U1.AVCC, U1.AREF, VCC1.+
  N2: U1.GND#7, C2.1, C3.2, VCC1.-
  N3: U1.XLAT1, C2.2, Y1.2
  N4: U1.XLAT2, C3.1, Y1.1

notes:
  Capacitors: 22 pF
  Crystal: 16 MHz
  Varje källa av 5 Volt.
  OBS: chippen kan tar
  1.8 och 5.5 Volt
  Chippen har skåran på vänster sida
