# Fritzing sketch ky-038_microfon (saved by Fritzing 0.9.6b)
breadboards: 1

parts:
  Mic1 = KY-038
  Part1 = Arduino Uno (Rev3)
  LED1 = LED - 5mm [color="Green (555nm)" current=0.030 package="5 mm [THT]"]
  LED2 = LED - 5mm [color="Red (633nm)" current=0.030 package="5 mm [THT]"]
  J1 = Piezo Speaker
  R1 = Resistor [tolerance=±5% power=0.25 resistance=1000 package=THT]
  R2 = Resistor [tolerance=±5% power=0.25 resistance=1000 package=THT]
  R3 = Resistor [tolerance=±5% power=0.25 resistance=1000 package=THT]

nets:
  N1: Mic1.pin1, Part1.A0
  N2: Mic1.pin2, Part1.GND, R1.Pin_1, R2.Pin_1, R3.Pin_1
  N3: Mic1.pin3, Part1.5V
  N4: Part1.D11_PWM/MOSI, J1.pin2
  N5: Part1.D12/MISO, LED2.cathode
  N6: Part1.D13/SCK, LED1.cathode
  N7: LED1.anode, R1.Pin_0
  N8: LED2.anode, R3.Pin_0
  N9: J1.pin1, R2.Pin_0

custom parts:
  KY-038: ky-038 Microphone sound sensor module
