# Fritzing sketch multimeter (saved by Fritzing 1.0.1rc)

parts:
  P1 = Multimeter straight red probe
  P2 = Multimeter straight black probe
  OM1 = Multimeter (Ohmmeter)
  R1 = Resistor [tolerance=±5% power=0.25 resistance=220 package=THT]  # not connected
  P3 = Multimeter straight red probe
  P4 = Multimeter straight black probe
  R2 = Resistor [tolerance=±5% power=0.25 resistance=1k package=THT]
  OM2 = Multimeter (DC Current)
  VCC1 = Battery
  LED1 = LED - 5mm [color="Red (633nm)" current=0.030 package="5 mm [THT]"]  # not connected
  P5 = Multimeter straight red probe
  P6 = Multimeter straight black probe
  R3 = Resistor [tolerance=±5% power=0.25 resistance=1k package=THT]
  LED2 = LED - 5mm [color="Red (633nm)" current=0.030 package="5 mm [THT]"]
  VCC3 = Battery
  OM3 = Multimeter (DC Voltage)
  P7 = Multimeter straight red probe
  P8 = Multimeter straight black probe
  OM4 = Multimeter (Ohmmeter)

nets:
  N1: P1.Probe_meter_end, OM1.V_Probe
  N2: P2.Probe_meter_end, OM1.COM_Probe
  N3: P3.Probe_tip, P3.Probe_meter_end, P3.Probe_tip_2, OM2.A_Probe, VCC1.+
  N4: P4.Probe_meter_end, OM2.COM_Probe
  N5: R2.Pin_1, VCC1.-
  N6: P5.Probe_tip, P5.Probe_meter_end, P5.Probe_tip_2, LED2.anode, VCC3.+, OM3.V_Probe
  N7: P6.Probe_tip, P6.Probe_meter_end, P6.Probe_tip_2, R3.Pin_0, LED2.cathode, OM3.COM_Probe
  N8: R3.Pin_1, VCC3.-
  N9: P7.Probe_tip, P7.Probe_meter_end, P7.Probe_tip_2, P8.Probe_tip, P8.Probe_meter_end, OM4.COM_Probe, OM4.V_Probe
