# Fritzing sketch test_fritzing_sim (saved by Fritzing 1.0.6)
breadboards: 1

parts:
  Part1 = Arduino Uno (Rev3)
  M1 = DC Motor [voltage_(max)=6V voltage_(min)=3V]  # not connected
  LED1 = LED - 5mm [color="Red (633nm)" current=0.030A package="5 mm [THT]"]
  R1 = Resistor [tolerance=±5% power=0.25W resistance=220 package=THT]

nets:
  N1: Part1.D13/SCK, R1.Pin_1
  N2: Part1.GND, LED1.cathode
  N3: LED1.anode, R1.Pin_0

// code stored in the sketch: test_fritzing_sim.ino
void setup()
{
  pinMode(13, OUTPUT);
}

void loop()
{
  digitalWrite(13, HIGH);
  delay(1000);
  digitalWrite(13, LOW);
  delay(1000);
}
