# Fritzing sketch 05_blink_6 (saved by Fritzing 0.9.3b)
circuit board: 8.46667cm x 5.64444cm
breadboards: 2

parts:
  A1 = Arduino Uno (Rev3)
  R1 = Resistor [tolerance=±5% resistance=1k package=THT]
  R2 = Resistor [tolerance=±5% resistance=1k package=THT]
  Part2 = Arduino Uno (Rev3)
  LED7 = LED - 5mm [color="Red (633nm)" package="5 mm [THT]"]
  LED8 = LED - 5mm [color="Red (633nm)" package="5 mm [THT]"]
  LED9 = LED - 5mm [color="Red (633nm)" package="5 mm [THT]"]
  LED10 = LED - 5mm [color="Red (633nm)" package="5 mm [THT]"]
  LED11 = LED - 5mm [color="Red (633nm)" package="5 mm [THT]"]
  LED12 = LED - 5mm [color="Red (633nm)" package="5 mm [THT]"]
  R7 = Resistor [tolerance=±5% resistance=1k package=THT]
  R8 = Resistor [tolerance=±5% resistance=1k package=THT]
  R9 = Resistor [tolerance=±5% resistance=1k package=THT]
  R10 = Resistor [tolerance=±5% resistance=1k package=THT]
  R11 = Resistor [tolerance=±5% resistance=1k package=THT]
  R12 = Resistor [tolerance=±5% resistance=1k package=THT]
  LED13 = LED - 5mm [color="Red (633nm)" package="5 mm [THT]"]
  LED14 = LED - 5mm [color="Red (633nm)" package="5 mm [THT]"]

nets:
  N1: A1.GND, R1.Pin_0, R2.Pin_0
  N2: A1.D2, LED13.anode
  N3: A1.D3_PWM, LED14.anode
  N4: R1.Pin_1, LED14.cathode
  N5: R2.Pin_1, LED13.cathode
  N6: Part2.GND, R7.Pin_0, R8.Pin_0, R9.Pin_0, R10.Pin_0, R11.Pin_0, R12.Pin_0
  N7: Part2.D2, LED7.anode
  N8: Part2.D3_PWM, LED8.anode
  N9: Part2.D4, LED9.anode
  N10: Part2.D5_PWM, LED10.anode
  N11: Part2.D6_PWM, LED11.anode
  N12: Part2.D7, LED12.anode
  N13: LED7.cathode, R7.Pin_1
  N14: LED8.cathode, R8.Pin_1
  N15: LED9.cathode, R9.Pin_1
  N16: LED10.cathode, R10.Pin_1
  N17: LED11.cathode, R11.Pin_1
  N18: LED12.cathode, R12.Pin_1

notes:
  1000 Ohm
  Brun
  Svart
  Röd
  Guld
  1000 Ohm
  Brun Svart Röd Guld
