# Fritzing sketch 07_potmeter_och_joystick (saved by Fritzing 0.9.3b)
breadboards: 2

parts:
  Part1 = Arduino Uno (Rev3)
  R1 = Rotary Potentiometer (Small) [maximum_resistance=100kΩ package=THT]
  Part2 = Arduino Uno (Rev3)
  Part3 = Thumb Joystick

nets:
  N1: Part1.A0, R1.wiper
  N2: Part1.5V, R1.leg1
  N3: Part1.GND, R1.leg2
  N4: Part2.A0, Part3.VERT
  N5: Part2.A1, Part3.HORZ
  5V: Part2.5V, Part3.VCC
  GND: Part2.GND, Part3.GND
